# Fritzing sketch schima (saved by Fritzing 0.9.3b)

parts:
  U1 = atmega328 [package=dip]
  XTAL1 = Crystal [frequency="16 Mhz" package=SMD]
  C1 = Capacitor [package=cap-pth-small2]
  C2 = Capacitor [package=cap-pth-small2]
  U2 = AVR 10-pin ICSP Header [package="avr icsp"]
  J1 = Piezo Speaker
  S1 = SWITCH-MOMENTARY-2 [package=tactile-pth-12mm]
  D1 = LTE-302 [package=lte-302]
  R1 = Resistor [tolerance=±5% resistance=220 package="2512 [SMD]"]

nets:
  N1: U1.RESET, U2.5
  N2: U1.D2, D1.A
  N3: U1.D3_(PWM), J1.pin2
  N4: U1.VCC, U2.2
  N5: U1.XLAT1, XTAL1.pin_0, C1.1
  N6: U1.XLAT2, XTAL1.pin_1, C2.1
  N7: U1.D11_(PWM), U2.1
  N8: U1.D12, U2.9
  N9: U1.D13, U2.7
  N10: U1.AVCC, U1.AREF, C1.2, C2.2, U2.10, J1.pin1, S1.2, R1.Pin_0
  N11: U1.A3, S1.1
  N12: D1.C, R1.Pin_1
